# Fritzing sketch Light_Controlled_Granular_Synth (saved by Fritzing 0.7.10b)
breadboards: 2

parts:
  Arduino1 = Arduino
  LCD1 = LCD screen
  SPKR1 = Loudspeaker
  S1 = Pushbutton [package="[THT]"]
  R1 = Rotary Potentiometer (Small) [maximum_resistance=100kΩ]
  R2 = Rotary Potentiometer (Small) [maximum_resistance=100kΩ]
  R3 = Rotary Potentiometer (Small) [maximum_resistance=100kΩ]
  R4 = Photocell (LDR) [package=THT]
  R5 = Photocell (LDR) [package=THT]
  R6 = Photocell (LDR) [package=THT]
  R7 = Resistor [tolerance=±5% resistance=10k package=THT]
  R8 = Resistor [tolerance=±5% resistance=220 package=THT]
  R9 = Resistor [tolerance=±5% resistance=10k package=THT]
  R10 = Resistor [tolerance=±5% resistance=10k package=THT]
  R11 = Resistor [tolerance=±5% resistance=10k package=THT]

nets:
  N1: Arduino1.D12, LCD1.RS
  N2: Arduino1.D11, LCD1.E
  N3: Arduino1.D9, LCD1.DB4
  N4: Arduino1.D8, S1.Pin_1, S1.Pin_2, R7.Pin_1
  N5: Arduino1.D6, LCD1.DB5
  N6: Arduino1.D5, LCD1.DB6
  N7: Arduino1.D4, LCD1.DB7
  N8: Arduino1.D3, SPKR1.pin2
  +5V: Arduino1.+5V, LCD1.VDD, S1.Pin_3, S1.Pin_4, R1.leg2, R2.leg1, R3.leg1, R5.pin_1, R6.pin_1, R8.Pin_0, R9.Pin_0
  GND: Arduino1.GND, LCD1.VSS, LCD1.R/W, LCD1.LED-, SPKR1.pin1, R1.leg1, R7.Pin_0, R11.Pin_1
  N9: Arduino1.A0, R2.wiper
  N10: Arduino1.A1, R5.pin_0, R11.Pin_0
  N11: Arduino1.A2, R3.wiper
  N12: Arduino1.A3, R4.pin_1, R9.Pin_1
  N13: Arduino1.A5, R6.pin_0, R10.Pin_1
  N14: LCD1.V0, R1.wiper
  N15: LCD1.LED+, R8.Pin_1
  N16: R2.leg2, R3.leg2, R4.pin_0, R10.Pin_0

notes:
  'MAKE NOISE WITH THE NEW ARDUINO KIT' TUTORIAL
  Hey! This is the scheme for the tutorial you can see in this video: link
  We only used components from the new Arduino Starter Kit (except for the speaker)
  We started from two examples that come with the kit, the Light Theremin and the LCD Crystal Ball and we merged them with a cool Synth project to create a Light Controlled Granular Synth!
  You can download the Arduino code here: link
  by Alessandro Contini + Alberto Massa
  (Dec 2012)
  You better put a resistor before the speaker.
  The value of the resistor depends on the speaker you will use
